# Fritzing sketch sensor_Project (saved by Fritzing 0.9.3b)
breadboards: 1

parts:
  U1 = LCD-16X2 [package=lcd-16x2_noholes]  # not connected
  Part1 = Arduino Uno (Rev3)
  R1 = TRIMPOT [package=3386u]
  T1 = LM35 Temperature Sensor [package="TO92 [THT]"]  # not connected

nets:
  N1: Part1.5V, R1.CCW
  N2: Part1.GND, R1.CW

notes:
  16x2 LCD
  Potentiometer - to adjust contrast of LCD
  Temperature Sensor
  Orange Wires - Temp Sensor Connections
  Black Wires - Potentiometer connections
  Green Wires - 5V to + and GND to -
  Blue and Yellow Wires - Connectios for LCD
